// Logisim project ca_inn.circ as structural Verilog
module main (
  input  [11:0] Control_Word,
  input  in_2,
  input  [3:0] in_3,
  input  in_4,
  input  in_5,
  input  [3:0] in_6,
  input  [1:0] in_7,
  input  [1:0] in_8,
  input  in_9,
  input  in_10,
  input  in_11,
  output c_out,
  output [3:0] OUTPUT,
  output [2:0] out_14,
  output [2:0] out_15,
  output [2:0] out_16,
  output [2:0] out_17
);

  wire CLOCK_out;
  wire [3:0] adder_1_out, adder_2_out, adder_3_out, adder_4_out, adder_5_out, demultiplexer_1_out0,
       demultiplexer_1_out1, demultiplexer_1_out2, demultiplexer_1_out3, demultiplexer_1_out4,
       demultiplexer_1_out5, demultiplexer_1_out6, demultiplexer_1_out7, multiplexer_1_out,
       multiplexer_2_out, not_1_out, OR_out, R0_input_q, R1_q, R2_q, R3_q, R4_q, R5_q, R6_q, R7_q,
       shifter_1_out, shifter_2_out;

  Demultiplexer #(.select(3), .width(4)) demultiplexer_1 (
    .out0(demultiplexer_1_out0), .out1(demultiplexer_1_out1), .out2(demultiplexer_1_out2),
    .out3(demultiplexer_1_out3), .out4(demultiplexer_1_out4), .out5(demultiplexer_1_out5),
    .out6(demultiplexer_1_out6), .out7(demultiplexer_1_out7), .in(OUTPUT), .sel(Control_Word[5:3]), .en(in_11));
  Clock CLOCK (.out(CLOCK_out));
  Register #(.width(4)) R0_input (.D(demultiplexer_1_out0), .en(in_2), .Q(R0_input_q), .clk(CLOCK_out));  // open: clr
  Register #(.width(4)) R1 (.D(demultiplexer_1_out1), .en(in_2), .Q(R1_q), .clk(CLOCK_out));  // open: clr
  Register #(.width(4)) R2 (.D(demultiplexer_1_out2), .en(in_2), .Q(R2_q), .clk(CLOCK_out));  // open: clr
  Register #(.width(4)) R3 (.D(demultiplexer_1_out3), .en(in_2), .Q(R3_q), .clk(CLOCK_out));  // open: clr
  Register #(.width(4)) R4 (.D(demultiplexer_1_out4), .en(in_2), .Q(R4_q), .clk(CLOCK_out));  // open: clr
  Register #(.width(4)) R5 (.D(demultiplexer_1_out5), .en(in_2), .Q(R5_q), .clk(CLOCK_out));  // open: clr
  Register #(.width(4)) R6 (.D(demultiplexer_1_out6), .en(in_2), .Q(R6_q), .clk(CLOCK_out));  // open: clr
  Register #(.width(4)) R7 (.D(demultiplexer_1_out7), .en(in_2), .Q(R7_q), .clk(CLOCK_out));  // open: clr
  Multiplexer #(.select(3), .width(4)) multiplexer_1 (
    .in0(R0_input_q), .in1(R1_q), .in2(R2_q), .in3(R3_q), .in4(R4_q), .in5(R5_q), .in6(R6_q), .in7(R7_q),
    .out(multiplexer_1_out), .sel(Control_Word[11:9]), .en(in_9));
  Multiplexer #(.select(3), .width(4)) multiplexer_2 (
    .in0(R0_input_q), .in1(R1_q), .in2(R2_q), .in3(R3_q), .in4(R4_q), .in5(R5_q), .in6(R6_q), .in7(R7_q),
    .out(multiplexer_2_out), .sel(Control_Word[8:6]), .en(in_10));
  assign not_1_out = ~multiplexer_2_out;  // NOT_Gate not_1, 4 bits wide
  assign OR_out = multiplexer_2_out | multiplexer_1_out;  // OR_Gate OR, 4 bits wide
  Adder #(.width(4)) adder_1 (.a(multiplexer_1_out), .b(in_3), .out(adder_1_out));  // open: cin, cout
  Adder #(.width(4)) adder_2 (.a(multiplexer_2_out), .b(in_3), .out(adder_2_out));  // open: cin, cout
  Adder #(.width(4)) adder_3 (
    .a(multiplexer_1_out), .b(multiplexer_2_out), .out(adder_3_out), .cout(c_out));  // open: cin
  Adder #(.width(4)) adder_4 (.a(multiplexer_1_out), .b(not_1_out), .out(adder_4_out), .cin(in_4));  // open: cout
  Adder #(.width(4)) adder_5 (.a(multiplexer_1_out), .b(in_6), .out(adder_5_out));  // open: cin, cout
  Shifter #(.width(4)) shifter_1 (.in(multiplexer_1_out), .\dist (in_7), .out(shifter_1_out));
  Shifter #(.width(4), .shift("lr")) shifter_2 (.in(multiplexer_1_out), .\dist (in_8), .out(shifter_2_out));
  Multiplexer #(.select(3), .width(4)) multiplexer_3 (
    .in0(OR_out), .in1(adder_1_out), .in2(adder_2_out), .in3(adder_3_out), .in4(adder_4_out),
    .in5(adder_5_out), .in6(shifter_1_out), .in7(shifter_2_out), .out(OUTPUT), .sel(Control_Word[2:0]),
    .en(in_5));

  assign out_14 = Control_Word[2:0];
  assign out_15 = Control_Word[8:6];
  assign out_16 = Control_Word[5:3];
  assign out_17 = Control_Word[11:9];

  // Notes on the sheet:
  //   CA Innovative Assignment
  //   General Register Organisation
  //   A
  //   B
  //   20BCE052 Dev Bhatt
  //   20BCE057 Devasy Patel
  //   20BCE064 Dhyan Patel
  //   B
  //   A
  //   INC A
  //   INC B
  //   ADDITION
  //   SUB
  //   DEC A
  //   SHL A
  //   SHR A
endmodule
